// Logisim project Lab8.circ as structural Verilog: 1 circuit, main circuit main
module main (
  input  Write,
  output [7:0] ByteReader
);

  wire clock_1_out;
  wire [7:0] adder_1_out, register_1_q;

  Clock clock_1 (.out(clock_1_out));
  Register register_1 (.D(adder_1_out), .en(Write), .clk(clock_1_out), .Q(register_1_q));  // open: clr
  RAM memory (.addr(register_1_q), .we(1'b0), .oe(1'b1), .clk(clock_1_out), .dout(ByteReader));  // open: din
  Adder adder_1 (.a(register_1_q), .b(8'h1), .out(adder_1_out));  // open: cin, cout

  // Notes on the sheet:
  //   Kevin Wittlinger
  //   add
  //   M3
  //   M2
  //   I pledge my honor that I have abided by the Stevens honor system
  //   C1
  //   PC
  //   adder
endmodule
