// Logisim project project2.circ as structural Verilog: 1 circuit, main circuit main
module main (
  input  in_1,
  input  [7:0] in_2,
  input  in_3,
  input  in_4,
  input  RegWrite,
  output out_6
);

  wire and_1_out, and_2_out, and_3_out, and_4_out, clock_1_out, decoder_1_out0, decoder_1_out1,
       decoder_1_out2, decoder_1_out3;
  wire [3:0] multiplexer_3_out, multiplexer_3_out_2;
  wire [7:0] adder_1_out, adder_2_out, multiplexer_1_out, multiplexer_2_out, PC_q, subtractor_1_out, X0_q,
       X1_q, X2_q, X3_q;
  wire [7:1] ram_1_dout;

  Clock clock_1 (.out(clock_1_out));
  Register PC (.D(adder_1_out), .en(in_1), .clk(clock_1_out), .Q(PC_q));  // open: clr
  RAM #(.asyncread("true")) ram_1 (
    .addr(adder_1_out), .we(in_3), .oe(in_4), .clk(clock_1_out), .dout({ram_1_dout, out_6}));  // open: din
  Adder adder_1 (.a(PC_q), .b(in_2), .out(adder_1_out));  // open: cin, cout
  Decoder #(.select(2)) decoder_1 (
    .out0(decoder_1_out0), .out1(decoder_1_out1), .out2(decoder_1_out2), .out3(decoder_1_out3),
    .sel(ram_1_dout[2:1]));  // open: en
  and and_1 (and_1_out, decoder_1_out0, RegWrite);
  and and_2 (and_2_out, decoder_1_out1, RegWrite);
  and and_3 (and_3_out, decoder_1_out2, RegWrite);
  and and_4 (and_4_out, decoder_1_out3, RegWrite);
  Register X0 (.D({multiplexer_3_out_2, multiplexer_3_out}), .en(and_1_out), .clk(clock_1_out), .Q(X0_q));  // open: clr
  Register X1 (.D({multiplexer_3_out_2, multiplexer_3_out}), .en(and_2_out), .clk(clock_1_out), .Q(X1_q));  // open: clr
  Register X2 (.D({multiplexer_3_out_2, multiplexer_3_out}), .en(and_3_out), .clk(clock_1_out), .Q(X2_q));  // open: clr
  Register X3 (.D({multiplexer_3_out_2, multiplexer_3_out}), .en(and_4_out), .clk(clock_1_out), .Q(X3_q));  // open: clr
  Multiplexer #(.select(2), .width(8)) multiplexer_1 (
    .in0(X0_q), .in1(X1_q), .in2(X2_q), .in3(X3_q), .out(multiplexer_1_out), .sel(ram_1_dout[6:5]));
  Multiplexer #(.select(2), .width(8)) multiplexer_2 (
    .in0(X0_q), .in1(X1_q), .in2(X2_q), .in3(X3_q), .out(multiplexer_2_out), .sel(ram_1_dout[4:3]));
  Adder adder_2 (.a(multiplexer_1_out), .b(multiplexer_2_out), .out(adder_2_out));  // open: cin, cout
  Subtractor subtractor_1 (.a(multiplexer_1_out), .b(multiplexer_2_out), .out(subtractor_1_out));  // open: bin, bout
  Multiplexer #(.width(8)) multiplexer_3 (
    .in0(adder_2_out), .in1(subtractor_1_out), .out({multiplexer_3_out_2, multiplexer_3_out}),
    .sel(ram_1_dout[7]));
  Hex_Digit_Display hex_digit_display_1 (.value(multiplexer_3_out_2));  // open: dp
  Hex_Digit_Display hex_digit_display_2 (.value(multiplexer_3_out));  // open: dp

  // Notes on the sheet:
  //   in_1: initial=0x1
  //   in_4: initial=0x1
  //   in_2: initial=0x1
  //   RegWrite: initial=0x1
  //   RegDataW
  //   WriteReg
  //   Jaran Binning and Kevin Wittlinger
  //   I pledge my honor that I have abided by the Stevens Honor System
  //   CPU name: Todd
  //   RegData1
  //   ReadReg1
  //   RegData2
  //   ReadReg2
endmodule
